# Fritzing sketch analog-temp-LM335A (saved by Fritzing 0.8.0b)
breadboards: 1

parts:
  o_i = mystery part, 2 pins [chip_label=DATA-IN]
  +_- = mystery part, 2 pins [chip_label=PWR-OUT]
  i_o = mystery part, 2 pins [chip_label=DATA-OUT]
  R2 = Resistor [tolerance=±5% resistance=10k package="0805 [SMD]"]
  PWR = smd LED [color="Red (633nm)" package="0805 [SMD]"]
  TEMP_SENSOR = SO08 [chip_label=IC package=SO]
  R3 = Resistor [tolerance=±5% resistance=220 package="0805 [SMD]"]
  C1 = Electrolytic Capacitor [capacitance="1 μF" package="0405 [SMD, electrolytic]"]
  -_+ = mystery part, 2 pins [chip_label=PWR-IN]

nets:
  N1: o_i.pin1, i_o.pin1, TEMP_SENSOR.8, R3.Pin_0
  N2: o_i.pin2, i_o.pin2
  N3: +_-.pin1, R2.Pin_1, R3.Pin_1, C1.+, -_+.pin1
  N4: +_-.pin2, PWR.cathode, -_+.pin2
  N5: R2.Pin_0, PWR.anode

notes:
  In this example, a pushbutton is used as a digital input and an LED is a digital output. Related example: http://arduino.cc/en/Tutorial/Button
  LM335a
