# Fritzing sketch digital-output-WS812 (saved by Fritzing 0.8.0b)
breadboards: 1

parts:
  +_- = mystery part, 2 pins [chip_label=PWR-IN]
  o_i = mystery part, 2 pins [chip_label=DATA-IN]
  +_-_2 = mystery part, 2 pins [chip_label=PWR-OUT]
  i_o = mystery part, 2 pins [chip_label=DATA-OUT]
  Pad2 = Pad [width=1.22296296296297 height=3.19851851851851 connect=center]  # not connected
  Pad1 = Pad [width=1.22296296296297 height=3.19851851851851 connect=center]  # not connected
  Pad4 = Pad [width=1.22296296296297 height=3.19851851851851 connect=center]  # not connected
  Pad3 = Pad [width=1.22296296296297 height=3.19851851851851 connect=center]  # not connected
  LED1 = WS2812
  C1 = Ceramic Capacitor [capacitance=100nF package="0805 [SMD, multilayer]"]

nets:
  N1: +_-.pin1, LED1.GND, C1.1
  VCC: +_-.pin2, +_-_2.pin1, LED1.VCC, LED1.VDD, C1.0
  N2: o_i.pin1, i_o.pin2
  N3: o_i.pin2, LED1.DI
  N4: i_o.pin1, LED1.DO

notes:
  In this example, a pushbutton is used as a digital input and an LED is a digital output. Related example: http://arduino.cc/en/Tutorial/Button
  WS2812
  RGB-Led
  r0.1

custom parts:
  WS2812: Intelligent control LED integrated light source.
