# Fritzing sketch digital-temp-DS18B20 (saved by Fritzing 0.9.2b)
circuit board: 2.92478cm x 5.58617cm
breadboards: 1

parts:
  +_- = mystery part, 2 pins [chip_label=PWR-IN]
  o_i = mystery part, 2 pins [chip_label=DATA-IN]
  +_-_2 = mystery part, 2 pins [chip_label=PWR-OUT]
  i_o = mystery part, 2 pins [chip_label=DATA-OUT]
  R2 = Resistor [tolerance=±5% resistance=10k package="0805 [SMD]"]
  PWR = smd LED [color="Red (633nm)" package="0805 [SMD]"]
  Temperature = mystery part, 3 pins [chip_label=?]
  PWR1 = smd LED [color="Red (633nm)" package="0805 [SMD]"]
  Pad8 = Pad [width=2 height=3.7 connect=center]  # not connected
  Pad9 = Pad [width=2 height=3.7 connect=center]  # not connected

nets:
  N1: +_-.pin1, +_-_2.pin2, PWR.cathode, Temperature.pin1
  N2: +_-.pin2, +_-_2.pin1, R2.Pin_1, Temperature.pin3, PWR1.anode
  N3: o_i.pin1, i_o.pin2, Temperature.pin2, PWR1.cathode
  N4: o_i.pin2, i_o.pin1
  N5: R2.Pin_0, PWR.anode

notes:
  In this example, a pushbutton is used as a digital input and an LED is a digital output. Related example: http://arduino.cc/en/Tutorial/Button
  DS18B20
  r0.2
