# Fritzing sketch Display-I2C-8x2LCD (saved by Fritzing 0.8.0b)
breadboards: 1

parts:
  J2 = female pin header, 5 pins [form="♀ (female)"]
  R1 = Trimmer Potentiometer [maximum_resistance=10kΩ package=THT]
  MCP9808 = MCP9808-SSOP20 [part_number=MCP9808-E/SS chip_label=IC package=SSOP20]
  Pad1 = Pad [width=1.61270647619049 height=0.56444565396826 connect=center]
  Pad2 = Pad [width=1.61270647619049 height=0.56444565396826 connect=center]  # not connected
  Pad3 = Pad [width=1.61270647619049 height=0.56444565396826 connect=center]
  Pad4 = Pad [width=1.61270647619049 height=0.56444565396826 connect=center]
  Pad5 = Pad [width=1.61270647619049 height=0.56444565396826 connect=center]
  Pad6 = Pad [width=1.61270647619049 height=0.56444565396826 connect=center]
  Pad7 = Pad [width=1.61270647619049 height=0.56444565396826 connect=center]  # not connected
  Pad8 = Pad [width=1.61270647619049 height=0.56444565396826 connect=center]  # not connected
  Pad9 = Pad [width=1.61270647619049 height=0.56444565396826 connect=center]
  I2C_LCD_Adaptor = LCD screen
  c_d = female pin header, 2 pins [form="♀ (female)"]
  +_- = female pin header, 2 pins [form="♀ (female)"]
  C1 = Ceramic Capacitor [capacitance=100nF package="0805 [SMD, multilayer]"]
  IC1 = RT9361BGE [chip_label=IC package=SMD]
  C2 = Ceramic Capacitor [capacitance=100nF package="0805 [SMD, multilayer]"]
  C3 = Ceramic Capacitor [capacitance=100nF package="0805 [SMD, multilayer]"]

nets:
  N1: J2.pin1, MCP9808.VSS
  VCC: J2.pin2, R1.leg1, MCP9808.RESET, MCP9808.VCC, Pad9.pad, +_-.pin2, IC1.VIN, C2.0
  N2: J2.pin3, MCP9808.INT
  N3: J2.pin4, MCP9808.SDA, c_d.pin1
  N4: J2.pin5, MCP9808.SCL, c_d.pin2
  N5: R1.wiper, I2C_LCD_Adaptor.V0
  N6: R1.leg2, MCP9808.A0, Pad3.pad, Pad6.pad
  N7: MCP9808.A2, Pad1.pad, Pad4.pad
  N8: MCP9808.A1, Pad5.pad
  N9: MCP9808.GP0, I2C_LCD_Adaptor.DB4
  N10: MCP9808.GP1, I2C_LCD_Adaptor.DB5
  N11: MCP9808.GP2, I2C_LCD_Adaptor.DB6
  N12: MCP9808.GP3, I2C_LCD_Adaptor.DB7
  N13: MCP9808.GP4, I2C_LCD_Adaptor.E
  N14: MCP9808.GP5, I2C_LCD_Adaptor.RS
  N15: I2C_LCD_Adaptor.VSS, I2C_LCD_Adaptor.R/W, I2C_LCD_Adaptor.LED-, +_-.pin1
  N16: I2C_LCD_Adaptor.VDD, I2C_LCD_Adaptor.LED+, IC1.VOUT, C3.0
  N17: C1.0, IC1.CP
  N18: C1.1, IC1.CN

notes:
  - + i d c
  Clixx.io
  I2C LCD Adaptor
  (c) 2013 clixx.io

custom parts:
  RT9361BGE: Richtek RT936BGE DC-DC Convertor
