# Fritzing sketch power-hbridge-TA8050p (saved by Fritzing 0.9.2b)
circuit board: 2.92478cm x 5.58617cm
breadboards: 1

parts:
  f_r = female pin header, 2 pins [form="♀ (female)"]
  +_- = female pin header, 2 pins [form="♀ (female)"]
  +_-_2 = Screw terminal - 2 pins [package=THT]
  -_+ = Screw terminal - 2 pins [package=THT]
  U3 = mystery part, 7 pins [chip_label=?]
  U5 = AMS1117 Voltage Regulator [package=SOT223]
  Power = female pin header, 2 pins [form="♀ (female)"]
  C1 = Tantalum Capacitor [capacitance=1μF package="A 3216 [SMD, tantalum]"]

nets:
  N1: f_r.pin1, U3.pin1
  N2: f_r.pin2, U3.pin2
  N3: +_-.pin1, U5.output_voltage, C1.+
  GND: +_-.pin2, +_-_2.pin1, U3.pin4, U5.GND, C1.-
  N4: +_-_2.pin2, Power.pin1
  N5: -_+.pin1, U3.pin5
  N6: -_+.pin2, U3.pin3
  N7: U3.pin7, U5.input_voltage, Power.pin2

notes:
  Motor >>
  Power <<
  TA8050
  Motor Driver
  r0.3

custom parts:
  AMS1117 Voltage Regulator: 5V DC Voltage Regulator
