# Fritzing sketch power-mosfet-n (saved by Fritzing 0.9.2b)
circuit board: 2.92478cm x 5.58617cm
breadboards: 1

parts:
  o_i = female pin header, 2 pins [form="♀ (female)"]
  +_- = female pin header, 2 pins [form="♀ (female)"]
  R2 = Resistor [tolerance=±5% resistance=220 package="0805 [SMD]"]
  -_+ = Screw terminal - 2 pins [package=THT]
  -_+_2 = Screw terminal - 2 pins [package=THT]
  R5 = Resistor [tolerance=±5% resistance=1k package="0805 [SMD]"]
  Mosfet = Basic FET N-Channel [package="DPak [SMD]"]
  R6 = Resistor [tolerance=±5% resistance=220 package="0805 [SMD]"]
  R7 = Resistor [tolerance=±5% resistance=220 package="0805 [SMD]"]
  LED1 = smd LED [color="Red (633nm)" package="0805 [SMD]"]
  R8 = Resistor [tolerance=±5% resistance=220 package="0805 [SMD]"]
  D1 = Rectifier Diode [package="Melf DO-213 AA [SMD]"]

nets:
  N1: o_i.pin2, R7.Pin_1, R8.Pin_0
  N2: +_-.pin1, R2.Pin_0
  GND: +_-.pin2, -_+.pin1, Mosfet.source
  N3: R2.Pin_1, LED1.anode
  N4: -_+.pin2, -_+_2.pin1
  N5: -_+_2.pin2, D1.anode
  N6: R5.Pin_0, Mosfet.Gate, R8.Pin_1
  N7: Mosfet.drain, D1.cathode
  N8: R6.Pin_1, R7.Pin_0

notes:
  Ouput >>
  r0.1
  Power <<
  N-Channel
  ->>
  r0.2
