# Fritzing sketch Attiny-BT-HC05 (saved by Fritzing 0.8.0b)
breadboards: 1

parts:
  i_o = female pin header, 2 pins [form="♀ (female)"]
  Pad1 = Pad [width=2 height=1 connect=center]
  Pad2 = Pad [width=2 height=1 connect=center]  # not connected
  Pad3 = Pad [width=2 height=1 connect=center]  # not connected
  Pad4 = Pad [width=2 height=1 connect=center]  # not connected
  Pad5 = Pad [width=2 height=1 connect=center]  # not connected
  Pad6 = Pad [width=2 height=1 connect=center]  # not connected
  Pad7 = Pad [width=2 height=1 connect=center]  # not connected
  Pad8 = Pad [width=2 height=1 connect=center]  # not connected
  Pad9 = Pad [width=2 height=1 connect=center]  # not connected
  Pad10 = Pad [width=2 height=1 connect=center]  # not connected
  Pad11 = Pad [width=2 height=1 connect=center]  # not connected
  Pad12 = Pad [width=2 height=1 connect=center]
  Pad13 = Pad [width=2 height=1 connect=center]  # not connected
  Pad27 = Pad [width=2 height=1 connect=center]  # not connected
  Pad28 = Pad [width=2 height=1 connect=center]  # not connected
  Pad29 = Pad [width=2 height=1 connect=center]  # not connected
  Pad30 = Pad [width=2 height=1 connect=center]  # not connected
  Pad31 = Pad [width=2 height=1 connect=center]  # not connected
  Pad32 = Pad [width=2 height=1 connect=center]  # not connected
  Pad33 = Pad [width=2 height=1 connect=center]
  Pad34 = Pad [width=2 height=1 connect=center]  # not connected
  Pad35 = Pad [width=2 height=1 connect=center]
  Pad36 = Pad [width=2 height=1 connect=center]  # not connected
  Pad37 = Pad [width=2 height=1 connect=center]
  Pad38 = Pad [width=2 height=1 connect=center]  # not connected
  Pad39 = Pad [width=2 height=1 connect=center]  # not connected
  Pad40 = Pad [width=2 height=1 connect=center]  # not connected
  Pad41 = Pad [width=2 height=1 connect=center]
  Pad42 = Pad [width=2 height=1 connect=center]
  Pad43 = Pad [width=2 height=1 connect=center]  # not connected
  Pad44 = Pad [width=2 height=1 connect=center]  # not connected
  Pad45 = Pad [width=2 height=1 connect=center]  # not connected
  Pad46 = Pad [width=2 height=1 connect=center]  # not connected
  Pad47 = Pad [width=2 height=1 connect=center]
  Reset = Pad [width=1 height=1 connect=center]
  Pad49 = Pad [width=1 height=1 connect=center]
  -_+ = female pin header, 2 pins [form="♀ (female)"]
  R3 = Resistor [tolerance=±5% resistance=220 package="0805 [SMD]"]
  Pad50 = Pad [width=1 height=1 connect=center]
  Key = Pad [width=1 height=1 connect=center]

nets:
  N1: i_o.pin1, Pad35.pad
  N2: i_o.pin2, Pad41.pad
  N3: Pad1.pad, R3.Pin_0, Pad50.pad
  N4: Pad12.pad, Pad33.pad, Pad37.pad, -_+.pin1, R3.Pin_1
  N5: Pad42.pad, Key.pad
  N6: Pad47.pad, Reset.pad
  GND: Pad49.pad, -_+.pin2

notes:
  clixx.io
  HC-05 BlueTooth
  r0.1
