# Fritzing sketch esp8266-firmware-programming-adaptor (saved by Fritzing 0.7.12b)
breadboards: 1

parts:
  +_- = mystery part, 2 pins [chip_label=PWR-IN]
  d_c = mystery part, 2 pins [chip_label=DATA-IN]
  R2 = Resistor [tolerance=±5% resistance=10k package="0805 [SMD]"]
  PWR = smd LED [color="Red (633nm)" package="0805 [SMD]"]

nets:
  N1: +_-.pin1, d_c.pin2, PWR.cathode
  N2: +_-.pin2, d_c.pin1, R2.Pin_1
  N3: R2.Pin_0, PWR.anode

notes:
  In this example, a pushbutton is used as a digital input and an LED is a digital output. Related example: http://arduino.cc/en/Tutorial/Button
  ESP8266
  Firmware Upload
  Dongle
